# Fritzing sketch Gator_Eliminator_V4_SMD_R2 (saved by Fritzing 0.9.4)
circuit board: 5.6cm x 8.6cm

parts:
  J4 = Generic single row SMD female header - 4 pins [form="♀ (female)" package=THT]
  J3 = Generic single row SMD female header - 12 pins [form="♀ (female)" package=THT]
  J2 = Generic single row SMD female header - 8 pins [form="♀ (female)" package=THT]
  J1 = Generic single row SMD female header - 8 pins [form="♀ (female)" package=THT]  # not connected

nets:
  N1: J4.pin1, J4.pin2, J4.pin3, J4.pin4
  N2: J3.pin1, J3.pin2, J3.pin3, J3.pin4, J3.pin5, J3.pin6, J3.pin7, J3.pin8, J3.pin9, J3.pin10, J3.pin11, J3.pin12
  N3: J2.pin1, J2.pin2, J2.pin3, J2.pin4, J2.pin5, J2.pin6, J2.pin7, J2.pin8

notes:
  TX A7
  RX A6
  SDA A5
  SCL A4
  A3
  A2
  A1
  AUD A0
  Gator
  for
  Gator Eliminator
  Circuit Playground
  by Arnie Martin
  aka RealAbsurdity
  https://arnie.design
  github.com/RealAbsurdity
  Assemble with M3 screws
  and M3 brass standoffs
  Circuit
  GND
  VBUS
  I/O
  3.3v
  USB
  BATT
  DO NOT CONNECT
  TO DIGITAL I/O
  VBUS is 3.7 - 5v
  from BATT or USB
  WARNING!
  Playground
  Express
  Eliminator

custom parts:
  Generic single row SMD female header - 4 pins: Generic single row SMD female header
  Generic single row SMD female header - 12 pins: Generic single row SMD female header
  Generic single row SMD female header - 8 pins: Generic single row SMD female header
