# Fritzing sketch Robot_cat_entertainment_V1 (saved by Fritzing 0.9.4)

parts:
  Part1 = Adafruit Crickit for Circuit Playground Express [part_number="Adafruit #3093"]
  Part2 = Adafruit Circuit Playground Express [part_number="Adafruit #3333"]
  M1 = DC Motor
  PIR1 = PIR sensor
  PIR2 = PIR sensor
  PIR3 = PIR sensor
  PIR4 = PIR sensor
  BATT1 = 4xAA Switchable Battery Pack w/Bare Wire
  JACK1 = 2.1mm Barrel Jack with Terminal Block
  S1 = Limit Switch [package="Breakout Board"]
  3-pins_Hall_Effect_Sensor1 = mystery part, 3 pins [chip_label="Hall Effect Sensor"]
  3-pins_Hall_Effect_Sensor2 = mystery part, 3 pins [chip_label="Hall Effect Sensor"]

nets:
  N1: Part1.CPX_A0, Part2.D12_A0_SPEAKER
  N2: Part1.CPX_A1, Part2.D6_A1
  GND: Part1.GND, Part2.GND, PIR1.GND, PIR2.GND, PIR3.GND, PIR4.GND, S1.G, 3-pins_Hall_Effect_Sensor1.pin2, 3-pins_Hall_Effect_Sensor2.pin2
  N3: Part1.CPX_SCL, Part2.D3_A4_SCL
  N4: Part1.CPX_SDA, Part2.D2_A5_SDA
  N5: Part1.CPX_VOUT, Part2.VOUT
  N6: Part1.ANALOG1, PIR2.SIG
  VDD: Part1.3.3V, PIR1.VDD, PIR2.VDD, PIR3.VDD, PIR4.VDD, S1.V, 3-pins_Hall_Effect_Sensor1.pin3, 3-pins_Hall_Effect_Sensor2.pin3
  N7: Part1.ANALOG2, PIR4.SIG
  N8: Part1.ANALOG3, PIR3.SIG
  N9: Part1.ANALOG4, PIR1.SIG
  N10: Part1.ANALOG5, S1.S
  N11: Part1.ANALOG6, 3-pins_Hall_Effect_Sensor1.pin1
  N12: Part1.ANALOG7, 3-pins_Hall_Effect_Sensor2.pin1
  N13: Part1.MOTOR_1B_OUT, M1.pin_2
  N14: Part1.MOTOR_1A_OUT, M1.pin_1
  N15: BATT1.POS, BATT1.NEG, JACK1.POS, JACK1.NEG

custom parts:
  Adafruit Crickit for Circuit Playground Express: Sometimes we wonder if robotics engineers ever watch movies. If they did, they'd know that making robots into slaves always ends up in a robot rebellion. Why even go down that path? Here at Adafruit, we believe in making robots our friends! So if you find yourself wanting a companion, consider the robot. They're fun to program, and you can get creative with decorations. With that in mind, we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
  Adafruit Circuit Playground Express: Circuit Playground Express is the next step towards a perfect introduction to electronics and programming. We've taken the original Circuit Playground Classic and made it even better! Not only did we pack even more sensors in, we also made it even easier to program. You can now start your journey with Microsoft MakeCode block-based or Javascript programming. Then, you can use the same board to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
  4xAA Switchable Battery Pack w/Bare Wire: 4xAA Switchable Battery Pack with Bare Wire connection
  Limit Switch: Generic limit switch commonly found on 3D printers. Typical lever microswitch mounted on a PCB board with a 3 pin JST XH connector.
